# Fritzing sketch R05_N1 (saved by Fritzing 0.9.3b)
breadboards: 1

parts:
  Componente1 = Arduino Uno (Rev3)
  R1 = Resistor [tolerance=±5% power=0.25 resistance=220 package=THT]
  ponta1 = ponta prova  # not connected
  ponta2 = ponta prova  # not connected

nets:
  N1: Componente1.A0, R1.Pin_1
  N2: Componente1.D8, R1.Pin_0

custom parts:
  ponta prova: test leads condutivimeter
  ponta prova: test leads condutivimeter
