# Fritzing sketch R05_N2 (saved by Fritzing 0.9.3b)
breadboards: 1

parts:
  Componente1 = Arduino Uno (Rev3)
  LCD2 = LCD screen
  LCM1602_IIC2 = LCM1602 IIC [part_number="LCM1602 IIC" chip_label="LCM1602 IIC" package="DIP (Dual Inline) [THT]"]
  R1 = Resistor [tolerance=±5% power=0.25 resistance=220 package=THT]
  ponta1 = ponta prova  # not connected
  ponta2 = ponta prova  # not connected

nets:
  N1: Componente1.A0, R1.Pin_1
  N2: Componente1.A4/SDA, LCM1602_IIC2.SDA
  N3: Componente1.A5/SCL, LCM1602_IIC2.SCL
  N4: Componente1.D8, R1.Pin_0
  5V: Componente1.5V, LCM1602_IIC2.VCC
  GND: Componente1.GND, LCM1602_IIC2.GND
  VSS: LCD2.VSS, LCM1602_IIC2.VSS
  VDD: LCD2.VDD, LCM1602_IIC2.VDD
  N5: LCD2.V0, LCM1602_IIC2.V0
  N6: LCD2.RS, LCM1602_IIC2.RS
  N7: LCD2.R/W, LCM1602_IIC2.RW
  N8: LCD2.E, LCM1602_IIC2.E
  N9: LCD2.DB0, LCM1602_IIC2.D0
  N10: LCD2.DB1, LCM1602_IIC2.D1
  N11: LCD2.DB2, LCM1602_IIC2.D2
  N12: LCD2.DB3, LCM1602_IIC2.D3
  N13: LCD2.DB4, LCM1602_IIC2.D4
  N14: LCD2.DB5, LCM1602_IIC2.D5
  N15: LCD2.DB6, LCM1602_IIC2.D6
  N16: LCD2.DB7, LCM1602_IIC2.D7
  N17: LCD2.LED+, LCM1602_IIC2.A
  N18: LCD2.LED-, LCM1602_IIC2.K
  N19: LCM1602_IIC2.LED_A, LCM1602_IIC2.LED_B

custom parts:
  LCM1602 IIC: I2C-Module to use a 1602 or 2004 LCD on with the wire.h libory Serial LCD Modul
  ponta prova: test leads condutivimeter
  ponta prova: test leads condutivimeter
