# Fritzing sketch R05_N3 (saved by Fritzing 0.9.3b)
breadboards: 1

parts:
  Componente1 = Arduino Uno (Rev3)
  LCD2 = LCD screen
  SD_card_module2 = SD Card Module
  LCM1602_IIC2 = LCM1602 IIC [part_number="LCM1602 IIC" chip_label="LCM1602 IIC" package="DIP (Dual Inline) [THT]"]
  R1 = Resistor [tolerance=±5% power=0.25 resistance=220 package=THT]
  ponta1 = ponta prova  # not connected
  ponta2 = ponta prova

nets:
  N1: Componente1.A0, R1.Pin_1
  N2: Componente1.A4/SDA, LCM1602_IIC2.SDA
  N3: Componente1.A5/SCL, LCM1602_IIC2.SCL
  N4: Componente1.D8, R1.Pin_0
  N5: Componente1.D10_PWM/SS, SD_card_module2.CS
  N6: Componente1.D11_PWM/MOSI, SD_card_module2.MOSI
  N7: Componente1.D12/MISO, SD_card_module2.MISO
  N8: Componente1.D13/SCK, SD_card_module2.SCK
  N9: Componente1.D7, ponta2.ponta_prova
  5V: Componente1.5V, SD_card_module2.+5, LCM1602_IIC2.VCC
  GND: Componente1.GND, SD_card_module2.GND, LCM1602_IIC2.GND
  VSS: LCD2.VSS, LCM1602_IIC2.VSS
  VDD: LCD2.VDD, LCM1602_IIC2.VDD
  N10: LCD2.V0, LCM1602_IIC2.V0
  N11: LCD2.RS, LCM1602_IIC2.RS
  N12: LCD2.R/W, LCM1602_IIC2.RW
  N13: LCD2.E, LCM1602_IIC2.E
  N14: LCD2.DB0, LCM1602_IIC2.D0
  N15: LCD2.DB1, LCM1602_IIC2.D1
  N16: LCD2.DB2, LCM1602_IIC2.D2
  N17: LCD2.DB3, LCM1602_IIC2.D3
  N18: LCD2.DB4, LCM1602_IIC2.D4
  N19: LCD2.DB5, LCM1602_IIC2.D5
  N20: LCD2.DB6, LCM1602_IIC2.D6
  N21: LCD2.DB7, LCM1602_IIC2.D7
  N22: LCD2.LED+, LCM1602_IIC2.A
  N23: LCD2.LED-, LCM1602_IIC2.K
  N24: LCM1602_IIC2.LED_A, LCM1602_IIC2.LED_B

custom parts:
  SD Card Module: SD Card Module Slot Socket Reader For Arduino ARM MCU
  LCM1602 IIC: I2C-Module to use a 1602 or 2004 LCD on with the wire.h libory Serial LCD Modul
  ponta prova: test leads condutivimeter
  ponta prova: test leads condutivimeter
